# Fritzing sketch leds_wiring (saved by Fritzing 0.9.3b)

parts:
  Composant1 = Arduino Nano (Rev3.0)
  NEOPIXEL1 = Neopixel Strip -- Black (30/m)
  R1 = Resistor [tolerance=±5% resistance=480 package=THT]

nets:
  N1: Composant1.D6, R1.Pin_0
  GND: Composant1.GND, NEOPIXEL1.GND
  5V: Composant1.5V, NEOPIXEL1.+5V
  N2: NEOPIXEL1.Din, R1.Pin_1

notes:
  480Ω
  Plug on DI
  Do not plug on DO
  X
  Do not use more than 5 leds

custom parts:
  Neopixel Strip -- Black (30/m): These NeoPixel strips have 30 digitally-addressable pixel LEDs per meter and are very affordable and are only 12.5 mm wide, 10 mm if you remove the strip from the casing.
